// Logisim project projectLogisim.circ as structural Verilog: 1 circuit, main circuit main
module main (
);

  wire and_1_out, and_2_out, and_3_out, and_4_out, and_5_out, not_1_out, or_1_out, undriven, undriven_2,
       undriven_3, undriven_4, undriven_5, undriven_6, undriven_7, undriven_8;

  and and_1 (and_1_out, undriven, undriven_5);
  // NOT_Gate not_1 has open pins: in=open, out=not_1_out
  and and_2 (and_2_out, not_1_out, undriven_6);
  // NAND_Gate nand_1 is placed but not wired
  and and_3 (and_3_out, undriven_2, undriven_7);
  and and_4 (and_4_out, undriven_3, undriven_8);
  buf and_5 (and_5_out, undriven_4);  // AND_Gate
  or or_1 (or_1_out, and_1_out, and_5_out);

  // Notes on the sheet:
  //   A
  //   B
  //   C
  //   A
  //   B
  //   C
  //   A
  //   B'
  //   C '
  //   A
  //   B'
  //   C
  //   A'
  //   B'
  //   C
  //   AND OR Circuit
  //   NAND Circuit
  //   f(A,B,C)
endmodule
